# Fritzing sketch cantaeiroMp3Arduino (saved by Fritzing 0.9.3b)
breadboards: 1

parts:
  U1 = LM124-324 Quad Opamp [package="DIP (Dual Inline)"]
  Componente1 = Arduino Uno (Rev3) - ICSP
  R1 = Resistor [tolerance=±5% resistance=220 package="0402 [SMD]"]
  R2 = Photocell (LDR) [package=THT]
  R3 = Resistor [tolerance=±5% resistance=10k package="0402 [SMD]"]
  R4 = Resistor [tolerance=±5% resistance=10k package="0402 [SMD]"]
  R5 = Resistor [tolerance=±5% resistance=10k package="0402 [SMD]"]
  Componente2 = Soil Moisture Sensor

nets:
  N1: U1.1OUT, R4.Pin_0
  5V: U1.VCC+, Componente1.5V, R2.pin_1, R5.Pin_1, Componente2.VCC
  N2: U1.2OUT, R3.Pin_1
  N3: U1.3OUT, Componente1.A0
  N4: U1.3IN-, R4.Pin_1
  N5: U1.3IN+, R3.Pin_0, R5.Pin_0
  GND: U1.VCC-, Componente1.GND, R1.Pin_0, Componente2.GND
  N6: Componente1.A1, R1.Pin_1, R2.pin_0
  N7: Componente1.A2, Componente2.SIG

notes:
  versão toque e toca
