# Fritzing sketch Cantaeiro (saved by Fritzing 0.9.3b)
breadboards: 1

parts:
  Componente1 = Arduino Uno (Rev3)
  R1 = Resistor [tolerance=±5% resistance=3.3M package=THT]
  R2 = Resistor [tolerance=±5% resistance=1M package=THT]
  R3 = Resistor [tolerance=±5% resistance=470 package=THT]
  U2 = POT [package=3362u]
  R4 = Resistor [tolerance=±5% resistance=12k package=THT]
  U3 = LM124-324 Quad Opamp [package="DIP (Dual Inline)"]
  R5 = Photocell (LDR) [package=THT]
  Part1 = Soil Moisture Sensor
  R6 = Resistor [tolerance=±5% resistance=220 package=THT]

nets:
  N1: Componente1.A0, R1.Pin_0, U3.1OUT
  N2: Componente1.A1, R5.pin_1, R6.Pin_0
  N3: Componente1.A2, Part1.SIG
  3V3: Componente1.3V3, R3.Pin_1, U2.S, U3.VCC+, R5.pin_0, Part1.VCC
  GND: Componente1.GND, R4.Pin_0, U3.VCC-, Part1.GND, R6.Pin_1
  N4: R1.Pin_1, R2.Pin_1, U3.1IN-
  N5: R2.Pin_0, R3.Pin_0
  N6: U2.E, R4.Pin_1, U3.1IN+
